# Fritzing sketch rfid_olvaso (saved by Fritzing 0.9.6b)
breadboards: 1

parts:
  LED1 = LED - 5mm [color="Green (565nm)" current=0.030 package="5 mm [THT]"]
  R1 = Resistor [tolerance=±5% power=0.25 resistance=68 package=THT]  # not connected
  LED2 = LED - 5mm [color="Red (633nm)" current=0.030 package="5 mm [THT]"]
  S1 = Toggle Switch [package=THT]
  Part2 = Arduino Nano (Rev3.0)
  Part3 = RFID-RC522-v2
  R2 = Resistor [tolerance=±5% power=0.25 resistance=68 package=THT]

nets:
  GND: LED1.cathode, LED2.cathode, S1.L2, Part2.GND, Part3.GND
  N1: LED2.anode, R2.Pin_1
  5V: S1.L1, Part2.5V, Part3.3.3V
  N2: S1.COM, Part2.D2
  N3: Part2.D4, R2.Pin_0
  N4: Part2.D9, Part3.RST
  N5: Part2.D10, Part3.SDA
  N6: Part2.D11/MOSI, Part3.MOSI
  N7: Part2.D12/MISO, Part3.MISO
  N8: Part2.D13/SCK, Part3.SCK

custom parts:
  RFID-RC522-v2: A simple China made RFID-RC522 Reader; do check the pin labels, as this is a MFRC522 based clone.
